# Fritzing sketch TripleStirrerV1 (saved by Fritzing 0.9.5d)
stripboards: 1

parts:
  F1 = Fan - Ventilador [package=THT]
  F2 = Fan - Ventilador [package=THT]
  F3 = Fan - Ventilador [package=THT]
  12VDC = 2.1mm Barrel Jack with Terminal Block
  Q1 = PNP-Transistor [part_number=2N3906 package="TO92 [THT]"]
  Q2 = PNP-Transistor [part_number=2N3906 package="TO92 [THT]"]
  Q3 = PNP-Transistor [part_number=2N3906 package="TO92 [THT]"]
  Q4 = NPN-Transistor [part_number=2N3904 package="TO92 [THT]"]
  Q5 = NPN-Transistor [part_number=2N3904 package="TO92 [THT]"]
  Q6 = NPN-Transistor [part_number=2N3904 package="TO92 [THT]"]
  R1 = Resistor [tolerance=±5% resistance=1k package=THT]
  R2 = Resistor [tolerance=±5% resistance=1k package=THT]
  R3 = Resistor [tolerance=±5% resistance=1k package=THT]
  R4 = Resistor [tolerance=±5% resistance=1k package=THT]
  R5 = Resistor [tolerance=±5% resistance=1k package=THT]
  R6 = Resistor [tolerance=±5% resistance=1k package=THT]
  Part1 = Arduino Board Ethernet

nets:
  N1: F1.5V, Q1.B
  GND: F1.GND, F2.GND, F3.GND, 12VDC.NEG, Q4.E, Q5.E, Q6.E, Part1.GND
  N2: F2.5V, Q2.B
  N3: F3.5V, Q3.B
  N4: 12VDC.POS, Q1.C, Q2.C, Q3.C
  N5: Q1.E, R1.Pin_0
  N6: Q2.E, R3.Pin_0
  N7: Q3.E, R4.Pin_0
  N8: Q4.B, R2.Pin_0
  N9: Q4.C, R1.Pin_1
  N10: Q5.B, R5.Pin_0
  N11: Q5.C, R3.Pin_1
  N12: Q6.B, R6.Pin_0
  N13: Q6.C, R4.Pin_1
  N14: R2.Pin_1, Part1.D6_PWM
  N15: R5.Pin_1, Part1.D5_PWM
  N16: R6.Pin_1, Part1.D3_PWM

custom parts:
  Fan - Ventilador: Ventilador de 2 pines, se encuentra comunmente en computadoras de escritorio
